// Logisim project Avtomat_iskanjeNiza011.circ as structural Verilog: 1 circuit, main circuit main
module main (
  input  Enable,
  input  X,
  output Q1,
  output Y,
  output Q0
);

  wire clock_1_out, multiplexer_1_out, multiplexer_2_out, multiplexer_3_out, not_1_out, Q0_qn, Reset_out;

  Clock clock_1 (.out(clock_1_out));
  not not_1 (not_1_out, Q0);
  Multiplexer multiplexer_1 (.in0(1'b0), .in1(Q0_qn), .out(multiplexer_1_out), .sel(Q1), .en(Enable));
  Multiplexer #(.select(2)) multiplexer_2 (
    .in0(1'b0), .in1(1'b0), .in2(Q0), .in3(not_1_out), .out(multiplexer_2_out), .sel({X, Q1}), .en(Enable));
  Multiplexer multiplexer_3 (.in0(1'b1), .in1(multiplexer_1_out), .out(multiplexer_3_out), .sel(X), .en(Enable));
  Button Reset (.out(Reset_out));
  D_Flip_Flop u_Q1 (
    .clk(clock_1_out), .D(multiplexer_2_out), .Q(Q1), .en(Enable), .reset(Reset_out));  // open: Qn, preset
  D_Flip_Flop u_Q0 (
    .clk(clock_1_out), .D(multiplexer_3_out), .Q(Q0), .Qn(Q0_qn), .en(Enable), .reset(Reset_out));  // open: preset
  and and_1 (Y, Q1, Q0);
endmodule
