// Logisim project domaca1_2bitregister_nand.circ as structural Verilog: 3 circuits, main circuit main
module main (
  input  x1,
  input  x0,
  input  a,
  output y1,
  output y0
);

  wire clock_1_out, multiplexer_1_out, multiplexer_2_out;

  Multiplexer multiplexer_1 (.in0(y1), .in1(x1), .out(multiplexer_1_out), .sel(a));  // open: en
  Multiplexer multiplexer_2 (.in0(x0), .in1(y0), .out(multiplexer_2_out), .sel(a));  // open: en
  Clock clock_1 (.out(clock_1_out));
  D_Flip_Flop d_ff_1 (.clk(multiplexer_1_out), .D(clock_1_out), .Q(y1));  // open: Qn, preset, en, reset
  D_Flip_Flop d_ff_2 (.clk(multiplexer_2_out), .D(clock_1_out), .Q(y0));  // open: Qn, preset, en, reset
endmodule

module realizacijaZMux (
  input  x1,
  input  x0,
  input  a,
  output y1,
  output y0
);

  wire clock_1_out, multiplexer_1_out, multiplexer_2_out, Reset_out;

  Button Reset (.out(Reset_out));
  Multiplexer multiplexer_1 (.in0(x1), .in1(y0), .out(multiplexer_1_out), .sel(a));  // open: en
  Multiplexer multiplexer_2 (.in0(x0), .in1(y1), .out(multiplexer_2_out), .sel(a));  // open: en
  Clock clock_1 (.out(clock_1_out));
  D_Flip_Flop d_ff_1 (.clk(clock_1_out), .D(multiplexer_1_out), .Q(y1), .reset(Reset_out));  // open: Qn, preset, en
  D_Flip_Flop d_ff_2 (.clk(clock_1_out), .D(multiplexer_2_out), .Q(y0), .reset(Reset_out));  // open: Qn, preset, en
endmodule

module RealizacijaZNand (
  input  X1,
  input  A,
  input  X0,
  output Y1,
  output Y0
);

  wire clock_1_out, nand_1_out, nand_2_out, nand_3_out, nand_4_out, nand_5_out, nand_6_out, not_1_out,
       Reset_out;

  not not_1 (not_1_out, A);
  nand nand_1 (nand_1_out, X1, not_1_out);
  nand nand_2 (nand_2_out, A, Y0);
  nand nand_3 (nand_3_out, Y1, A);
  nand nand_4 (nand_4_out, not_1_out, X0);
  nand nand_5 (nand_5_out, nand_1_out, nand_2_out);
  nand nand_6 (nand_6_out, nand_3_out, nand_4_out);
  Clock clock_1 (.out(clock_1_out));
  Button Reset (.out(Reset_out));
  D_Flip_Flop d_ff_1 (.clk(clock_1_out), .D(nand_5_out), .Q(Y1), .reset(Reset_out));  // open: Qn, preset, en
  D_Flip_Flop d_ff_2 (.clk(clock_1_out), .D(nand_6_out), .Q(Y0), .reset(Reset_out));  // open: Qn, preset, en
endmodule
