// Logisim project MIPS Procesor.circ as structural Verilog: 4 circuits, main circuit main
module main (
  output [31:0] out_1,
  output [31:0] out_2,
  output [4:0] out_3,
  output [4:0] out_4,
  output [4:0] out_5,
  output [4:0] out_6
);

  wire ale_1_z, and_1_out, and_2_out, button_1_out, button_2_out, clock_1_out, not_1_out;
  wire [5:0] register_2_q;
  wire [7:0] rom_1_data;
  wire [10:0] register_2_q_2;
  wire [31:0] adder_1_out, adder_2_out, mipsprogramrom_1_p3, multiplexer_1_out, multiplexer_3_out,
       ram_1_data, register_1_q, registerfile_1_p6, registerfile_1_p7;

  Register #(.width(32)) register_1 (
    .D(multiplexer_1_out), .Q(register_1_q), .clk(clock_1_out), .clr(button_1_out));  // open: en
  Clock clock_1 (.out(clock_1_out));
  Button button_1 (.out(button_1_out));
  Adder #(.width(32)) adder_1 (.a(32'h4), .b(register_1_q), .out(adder_1_out));  // open: cin, cout
  Adder #(.width(32)) adder_2 (
    .a(adder_1_out), .b({{15{out_5[4]}}, out_5[3:0], register_2_q_2, 2'b00}), .out(adder_2_out));  // open: cin, cout
  Multiplexer #(.width(32)) multiplexer_1 (
    .in0(adder_1_out), .in1(adder_2_out), .out(multiplexer_1_out), .sel(and_1_out));  // open: en
  // MIPSProgramROM mipsprogramrom_1: pin names not known; wires that end beside it: register_1_q, adder_2_out, mipsprogramrom_1_p3, clock_1_out
  ROM #(.addrWidth(6)) rom_1 (.addr(register_2_q), .data(rom_1_data), .sel(1'b1));
  Multiplexer #(.width(32)) multiplexer_2 (
    .in0(ram_1_data), .in1(out_2), .out(out_1), .sel(rom_1_data[5]));  // open: en
  and and_1 (and_1_out, ~ale_1_z, rom_1_data[2]);  // AND_Gate
  Register #(.width(32)) register_2 (
    .D(mipsprogramrom_1_p3), .Q({register_2_q, out_3, out_4, out_5, register_2_q_2}), .clk(clock_1_out));  // open: en, clr
  not not_1 (not_1_out, rom_1_data[0]);
  // RegisterFile registerfile_1: pin names not known; wires that end beside it: out_1, rom_1_data[4], out_6, out_3, out_4, registerfile_1_p6, registerfile_1_p7
  and and_2 (and_2_out, not_1_out, rom_1_data[1]);
  Multiplexer #(.width(32)) multiplexer_3 (
    .in0(registerfile_1_p7), .in1({{17{out_5[4]}}, out_5[3:0], register_2_q_2}), .out(multiplexer_3_out),
    .sel(rom_1_data[7]));  // open: en
  ALE ale_1 (
    .Cin(1'b0), .X(registerfile_1_p6), .Y(multiplexer_3_out), .Shift(register_2_q_2[10:6]), .S2(1'b0),
    .S1(and_2_out), .S0(1'b0), .Z(ale_1_z), .O(out_2));  // open: N, C
  Multiplexer #(.width(5)) multiplexer_4 (.in0(out_4), .in1(out_5), .out(out_6), .sel(rom_1_data[6]));  // open: en
  RAM #(.addrWidth(24), .dataWidth(32)) ram_1 (
    .addr(out_2[23:0]), .data(ram_1_data), .sel(1'b1), .clk(clock_1_out), .ld(rom_1_data[3]),
    .clr(button_2_out));
  Button button_2 (.out(button_2_out));

  // Notes on the sheet:
  //   contents of rom_1 (hex, n*v repeats v):
  //   78 4*0 e 29*0 99
endmodule

module ALE (
  input  Cin,
  input  [31:0] X,
  input  [31:0] Y,
  input  [4:0] Shift,
  input  S2,
  input  S1,
  input  S0,
  output N,
  output Z,
  output C,
  output [31:0] O
);

  wire [30:0] adder_1_out;
  wire [31:0] adder_2_out, divider_1_out, multiplier_1_out, shifter_1_out, shifter_2_out, subtractor_1_out;

  Adder #(.width(32)) adder_1 (.a(X), .b(Y), .out({N, adder_1_out}), .cin(Cin), .cout(C));
  Adder #(.width(32)) adder_2 (.a(X), .b(32'h1), .out(adder_2_out));  // open: cin, cout
  Subtractor #(.width(32)) subtractor_1 (.a(X), .b(Y), .out(subtractor_1_out));  // open: bin, bout
  Multiplier #(.width(32)) multiplier_1 (.a(X), .b(Y), .out(multiplier_1_out));  // open: cin, cout
  Divider #(.width(32)) divider_1 (.a(X), .b(Y), .out(divider_1_out));  // open: upper, rem
  Comparator #(.width(32)) comparator_1 (.a(X), .b(Y), .eq(Z));  // open: gt, lt
  Shifter #(.width(32)) shifter_1 (.in(X), .\dist (Shift), .out(shifter_1_out));
  Shifter #(.width(32)) shifter_2 (.in(X), .\dist (Shift), .out(shifter_2_out));
  Multiplexer #(.select(3), .width(32)) multiplexer_1 (
    .in0({N, adder_1_out}), .in1(adder_2_out), .in2(subtractor_1_out), .in3(multiplier_1_out),
    .in4(divider_1_out), .in5(shifter_1_out), .in6(shifter_2_out), .out(O), .sel({S2, S1, S0}), .en(1'b1));  // open: in7

  // Notes on the sheet:
  //   ADD
  //   INC
  //   SUB
  //   MUL
  //   DIV
endmodule

module Fetch (
  output [31:0] out_1
);

  wire button_1_out, clock_1_out;
  wire [31:0] adder_1_out, mipsprogramrom_1_p2, register_1_q;

  Clock clock_1 (.out(clock_1_out));
  Button button_1 (.out(button_1_out));
  Register #(.width(32)) register_1 (
    .D(adder_1_out), .Q(register_1_q), .clk(clock_1_out), .clr(button_1_out));  // open: en
  Adder #(.width(32)) adder_1 (.a(32'h4), .b(register_1_q), .out(adder_1_out));  // open: cin, cout
  // MIPSProgramROM mipsprogramrom_1: pin names not known; wires that end beside it: register_1_q, mipsprogramrom_1_p2
  Register #(.width(32)) register_2 (.D(mipsprogramrom_1_p2), .Q(out_1), .clk(clock_1_out));  // open: en, clr
endmodule

module ALE_test (
  input  C0,
  input  [15:0] A,
  input  [15:0] B,
  input  [3:0] pomik,
  input  [2:0] F,
  output N,
  output Z,
  output C,
  output [15:0] Y
);

  // ALE ALE: pin names not known; wires that end beside it: C0, A, B, pomik, F[2], F[1], F[0], N, Z, C, Y
endmodule
