// Logisim project notWorkingStevecVaje11.circ as structural Verilog: 1 circuit, main circuit main
module main (
  output P
);

  wire button_1_out, clock_1_out;
  wire [2:0] _0_q, rom_1_data;

  Hex_Digit_Display hex_digit_display_1 (.value({1'b0, _0_q}));  // open: dp
  ROM #(.addrWidth(3), .dataWidth(4)) rom_1 (.addr(_0_q), .data({P, rom_1_data}), .sel(1'b1));
  Clock clock_1 (.out(clock_1_out));
  Button button_1 (.out(button_1_out));
  D_Flip_Flop _0 (.clk(clock_1_out), .D(rom_1_data[0]), .Q(_0_q[0]), .reset(button_1_out));  // open: Qn, preset, en
  J_K_Flip_Flop _1 (
    .clk(clock_1_out), .K(rom_1_data[1]), .Q(_0_q[1]), .reset(button_1_out));  // open: J, Qn, preset, en
  D_Flip_Flop _2 (.clk(clock_1_out), .D(rom_1_data[2]), .Q(_0_q[2]), .reset(button_1_out));  // open: Qn, preset, en

  // Notes on the sheet:
  //   contents of rom_1 (hex, n*v repeats v):
  //   9 a 9 e
endmodule
