// Logisim project sestevalnik_logisim.circ as structural Verilog: 2 circuits, main circuit main
module main (
  input  x3,
  input  x2,
  input  x1,
  input  x0,
  input  in_5,
  input  in_6,
  input  in_7,
  input  in_8,
  output Z,
  output s3,
  output out_11,
  output out_12,
  output out_13,
  output C,
  output N,
  output V
);

  wire ps_2_ci, ps_3_ci, ps_4_ci;

  PS ps_1 (.ci_1(ps_2_ci), .y(in_7), .x(x3), .Si(N), .Ci(C));
  PS ps_2 (.ci_1(ps_3_ci), .y(in_5), .x(x2), .Si(out_11), .Ci(ps_2_ci));
  xor xor_1 (V, ps_2_ci, C);
  PS ps_3 (.ci_1(ps_4_ci), .y(in_6), .x(x1), .Si(out_12), .Ci(ps_3_ci));
  PS ps_4 (.ci_1(1'b0), .y(in_8), .x(x0), .Si(out_13), .Ci(ps_4_ci));
  nor nor_1 (Z, N, out_11, out_12, out_13);

  assign s3 = N;
endmodule

module PS (
  input  ci_1,
  input  y,
  input  x,
  output Si,
  output Ci
);

  wire not_1_out;

  not not_1 (not_1_out, ci_1);
  Multiplexer #(.select(2)) multiplexer_1 (
    .in0(ci_1), .in1(not_1_out), .in2(not_1_out), .in3(ci_1), .out(Si), .sel({x, y}));  // open: en
  Multiplexer #(.select(2)) multiplexer_2 (
    .in0(1'b0), .in1(ci_1), .in2(ci_1), .in3(1'b1), .out(Ci), .sel({x, y}));  // open: en
endmodule
