// Logisim project vajaStevec2.circ as structural Verilog
module \xor  (
  input  A,
  output D1,
  output D0
);

  wire button_1_out, clock_1_out, d_ff_2_qn, xor_1_out, xor_2_out, xor_3_out;

  xor xor_1 (xor_1_out, D1, 1'b1);
  xor xor_2 (xor_2_out, A, D0);
  Button button_1 (.out(button_1_out));
  xor xor_3 (xor_3_out, xor_1_out, xor_2_out);
  Clock clock_1 (.out(clock_1_out));
  D_Flip_Flop d_ff_1 (.clk(clock_1_out), .D(xor_3_out), .Q(D1), .reset(button_1_out));  // open: Qn, preset, en
  D_Flip_Flop d_ff_2 (
    .clk(clock_1_out), .D(d_ff_2_qn), .Q(D0), .Qn(d_ff_2_qn), .reset(button_1_out));  // open: preset, en
endmodule

module mux (
  input  A,
  output Q1,
  output Q0
);

  wire button_1_out, clock_1_out, multiplexer_1_out, multiplexer_2_out, not_1_out;

  not not_1 (not_1_out, Q0);
  Multiplexer #(.select(2), .enable("false")) multiplexer_1 (
    .in0(not_1_out), .in1(Q0), .in2(Q0), .in3(not_1_out), .out(multiplexer_1_out), .sel({A, Q1}));
  Multiplexer #(.select(2)) multiplexer_2 (
    .in0(not_1_out), .in1(not_1_out), .in2(not_1_out), .in3(not_1_out), .out(multiplexer_2_out), .sel({A, Q1}));  // open: en
  Button button_1 (.out(button_1_out));
  Clock clock_1 (.out(clock_1_out));
  D_Flip_Flop d_ff_1 (.clk(clock_1_out), .D(multiplexer_1_out), .Q(Q1), .reset(button_1_out));  // open: Qn, preset, en
  D_Flip_Flop d_ff_2 (.clk(clock_1_out), .D(multiplexer_2_out), .Q(Q0), .reset(button_1_out));  // open: Qn, preset, en
endmodule
