// Logisim project vezje.circ as structural Verilog: 4 circuits, main circuit main
module main (
  input  [4:0] T_opt,
  input  [1:0] T1,
  input  [1:0] T2,
  input  [1:0] T3,
  input  [1:0] T4,
  input  [1:0] TH,
  input  P1,
  input  P2,
  input  P3,
  input  P4,
  input  V1,
  input  V2,
  input  V3,
  input  V4,
  output Ogrevanje1,
  output Ogrevanje2,
  output Ogrevanje3,
  output Ogrevanje4,
  output Okno1,
  output Okno2,
  output Okno3,
  output Okno4,
  output Vrata1,
  output Vrata2,
  output Vrata3,
  output Vrata4
);

  wire [6:0] controller_1_temperatura_display_bits;
  wire [13:7] controller_1_temperatura_display_bits_2;

  Controller controller_1 (
    .T_opt(T_opt), .Temperatura({TH, T4, T3, T2, T1}), .Vlaga({P4, {2{P2}}, P1}), .Pritisk({V4, V3, V2, V1}),
    .K_ogrevanje({Ogrevanje4, Ogrevanje3, Ogrevanje2, Ogrevanje1}), .K_okno({Okno4, Okno3, Okno2, Okno1}),
    .temperatura_display_bits({controller_1_temperatura_display_bits_2, controller_1_temperatura_display_bits}),
    .K_vrata({Vrata4, Vrata3, Vrata2, Vrata1}));
  _7_Segment_Display u_7_segment_display_1 (
    .g(controller_1_temperatura_display_bits[6]), .f(controller_1_temperatura_display_bits[5]),
    .a(controller_1_temperatura_display_bits[0]), .b(controller_1_temperatura_display_bits[1]),
    .e(controller_1_temperatura_display_bits[4]), .d(controller_1_temperatura_display_bits[3]),
    .c(controller_1_temperatura_display_bits[2]));  // open: dp
  _7_Segment_Display u_7_segment_display_2 (
    .g(controller_1_temperatura_display_bits_2[13]), .f(controller_1_temperatura_display_bits_2[12]),
    .a(controller_1_temperatura_display_bits_2[7]), .b(controller_1_temperatura_display_bits_2[8]),
    .e(controller_1_temperatura_display_bits_2[11]), .d(controller_1_temperatura_display_bits_2[10]),
    .c(controller_1_temperatura_display_bits_2[9]));  // open: dp

  assign P3 = P2;
endmodule

module BCD_to_7_segmented_decoder (
  input  D,
  input  C,
  input  B,
  input  A,
  output a_2,
  output b_2,
  output c_2,
  output d_2,
  output e,
  output f,
  output g
);

  wire and_1_out, and_2_out, and_3_out, and_4_out, and_5_out, and_6_out, and_7_out, and_8_out, and_9_out,
       and_10_out, and_11_out, and_12_out, and_13_out, and_14_out, and_15_out, and_16_out, not_1_out,
       not_2_out, not_3_out, not_4_out, not_5_out, not_6_out, not_7_out, not_8_out, not_9_out, not_10_out,
       not_11_out, not_12_out, not_13_out, not_14_out, not_15_out, not_16_out, not_17_out, not_18_out,
       not_19_out, not_20_out, not_21_out;

  not not_1 (not_1_out, C);
  and and_1 (and_1_out, not_1_out, not_2_out);
  not not_2 (not_2_out, A);
  and and_2 (and_2_out, C, A);
  not not_3 (not_3_out, C);
  not not_4 (not_4_out, B);
  and and_3 (and_3_out, not_4_out, not_5_out);
  not not_5 (not_5_out, A);
  and and_4 (and_4_out, B, A);
  not not_6 (not_6_out, B);
  or or_1 (c_2, not_6_out, A, C);
  not not_7 (not_7_out, C);
  and and_5 (and_5_out, not_7_out, not_8_out);
  not not_8 (not_8_out, A);
  not not_9 (not_9_out, C);
  and and_6 (and_6_out, not_9_out, B);
  and and_7 (and_7_out, B, not_10_out);
  not not_10 (not_10_out, A);
  not not_11 (not_11_out, B);
  and and_8 (and_8_out, C, not_11_out, A);
  not not_12 (not_12_out, C);
  and and_9 (and_9_out, not_12_out, not_13_out);
  not not_13 (not_13_out, A);
  and and_10 (and_10_out, B, not_14_out);
  not not_14 (not_14_out, A);
  not not_15 (not_15_out, B);
  and and_11 (and_11_out, not_15_out, not_16_out);
  not not_16 (not_16_out, A);
  and and_12 (and_12_out, C, not_17_out);
  not not_17 (not_17_out, B);
  and and_13 (and_13_out, C, not_18_out);
  not not_18 (not_18_out, A);
  not not_19 (not_19_out, C);
  and and_14 (and_14_out, not_19_out, B);
  and and_15 (and_15_out, C, not_20_out);
  not not_20 (not_20_out, B);
  and and_16 (and_16_out, C, not_21_out);
  not not_21 (not_21_out, A);
  or or_2 (a_2, and_1_out, B, and_2_out, D);
  or or_3 (b_2, not_3_out, and_3_out, and_4_out);
  or or_4 (d_2, and_5_out, and_6_out, and_7_out, and_8_out, D);
  or or_5 (e, and_9_out, and_10_out);
  or or_6 (f, and_11_out, and_12_out, and_13_out, D);
  or or_7 (g, and_14_out, and_15_out, and_16_out, D);
endmodule

// CTR
module Controller (
  input  [4:0] T_opt,
  input  [9:0] Temperatura,
  input  [3:0] Pritisk,
  input  [3:0] Vlaga,
  output [13:0] temperatura_display_bits,
  output [3:0] K_okno,
  output [3:0] K_ogrevanje,
  output [3:0] K_vrata
);

  wire [4:0] divider_1_out, divider_1_rem;

  Divider #(.width(5)) divider_1 (.a(T_opt), .b(5'b01010), .out(divider_1_out), .rem(divider_1_rem));  // open: upper
  BCD_to_7_segmented_decoder bcd_to_7_segmented_decoder_1 (
    .D(divider_1_out[3]), .C(divider_1_out[2]), .B(divider_1_out[1]), .A(divider_1_out[0]),
    .a_2(temperatura_display_bits[0]), .b_2(temperatura_display_bits[1]), .c_2(temperatura_display_bits[2]),
    .d_2(temperatura_display_bits[3]), .e(temperatura_display_bits[4]), .f(temperatura_display_bits[5]),
    .g(temperatura_display_bits[6]));
  BCD_to_7_segmented_decoder bcd_to_7_segmented_decoder_2 (
    .D(divider_1_rem[3]), .C(divider_1_rem[2]), .B(divider_1_rem[1]), .A(divider_1_rem[0]),
    .a_2(temperatura_display_bits[7]), .b_2(temperatura_display_bits[8]), .c_2(temperatura_display_bits[9]),
    .d_2(temperatura_display_bits[10]), .e(temperatura_display_bits[11]), .f(temperatura_display_bits[12]),
    .g(temperatura_display_bits[13]));
  ApartmentManager A1 (
    .Th1(Temperatura[9]), .Th0(Temperatura[8]), .Tb1(Temperatura[7]), .Tb0(Temperatura[7]), .P(Pritisk[3]),
    .V(Vlaga[3]), .Okno(K_okno[3]), .Heat(K_ogrevanje[3]), .Vrata(K_vrata[3]));
  ApartmentManager A2 (
    .Th1(Temperatura[9]), .Th0(Temperatura[8]), .Tb1(Temperatura[5]), .Tb0(Temperatura[4]), .P(Pritisk[2]),
    .V(Vlaga[2]), .Okno(K_okno[2]), .Heat(K_ogrevanje[2]), .Vrata(K_vrata[2]));
  ApartmentManager A3 (
    .Th1(Temperatura[9]), .Th0(Temperatura[8]), .Tb1(Temperatura[3]), .Tb0(Temperatura[2]), .P(Pritisk[1]),
    .V(Vlaga[1]), .Okno(K_okno[1]), .Heat(K_ogrevanje[1]), .Vrata(K_vrata[1]));
  ApartmentManager A4 (
    .Th1(Temperatura[9]), .Th0(Temperatura[8]), .Tb1(Temperatura[1]), .Tb0(Temperatura[0]), .P(Pritisk[0]),
    .V(Vlaga[0]), .Okno(K_okno[0]), .Heat(K_ogrevanje[0]), .Vrata(K_vrata[0]));

  assign Temperatura[6] = Temperatura[7];
endmodule

// AM
module ApartmentManager (
  input  Th1,
  input  Th0,
  input  Tb1,
  input  Tb0,
  input  P,
  input  V,
  output Okno,
  output Heat,
  output Vrata
);

  wire and_1_out, and_2_out, and_3_out, and_4_out, and_5_out, and_6_out, and_7_out, and_8_out, and_9_out,
       and_10_out, not_1_out, not_2_out, not_3_out, not_4_out, not_5_out, not_6_out, not_7_out, not_8_out,
       not_9_out;

  not not_1 (not_1_out, Th0);
  not not_2 (not_2_out, Tb1);
  not not_3 (not_3_out, Tb0);
  not not_4 (not_4_out, P);
  not not_5 (not_5_out, Tb1);
  not not_6 (not_6_out, Tb0);
  not not_7 (not_7_out, Th0);
  not not_8 (not_8_out, Tb1);
  not not_9 (not_9_out, Th1);
  and and_1 (and_1_out, Th0, Tb1);
  and and_2 (and_2_out, Th1, Tb0);
  and and_3 (and_3_out, Th1, Tb1);
  and and_4 (and_4_out, not_1_out, not_2_out, not_3_out, not_4_out);
  and and_5 (and_5_out, not_5_out, not_6_out, V);
  and and_6 (and_6_out, not_7_out, Tb1, P);
  and and_7 (and_7_out, Th0, not_8_out, V);
  and and_8 (and_8_out, Th1, Tb1);
  and and_9 (and_9_out, not_9_out, Tb0);
  and and_10 (and_10_out, Tb0, P);
  or or_1 (Vrata, and_1_out, and_2_out, and_3_out);
  or or_2 (Okno, and_4_out, and_5_out, and_6_out, and_7_out, and_8_out);
  or or_3 (Heat, and_9_out, and_10_out);
endmodule
