// Logisim project vmesna.circ as structural Verilog: 5 circuits, main circuit main
module main (
  input  [4:0] T_opt,
  input  [1:0] T1,
  input  [1:0] T2,
  input  [1:0] T3,
  input  [1:0] T4,
  input  P1,
  input  P2,
  input  P3,
  input  P4,
  input  V1,
  input  V2,
  input  V3,
  input  V4,
  output Ogrevanje1,
  output Ogrevanje2,
  output Ogrevanje3,
  output Ogrevanje4,
  output Okno1,
  output Okno2,
  output Okno3,
  output Okno4
);

  wire Reset_out;
  wire [13:0] controller_1_temperatura_display_bits;

  Controller controller_1 (
    .T_opt(T_opt), .Temperatura({T4, T3, T2, T1}), .Vlaga({P4, P3, P2, P1}), .Pritisk({V4, V3, V2, V1}),
    .Reset(Reset_out), .K_ogrevanje({Ogrevanje4, Ogrevanje3, Ogrevanje2, Ogrevanje1}),
    .K_okno({Okno4, Okno3, Okno2, Okno1}), .temperatura_display_bits(controller_1_temperatura_display_bits));
  Button Reset (.out(Reset_out));
  _7_Segment_Display u_7_segment_display_1 (
    .g(controller_1_temperatura_display_bits[12]), .f(controller_1_temperatura_display_bits[13]),
    .a(controller_1_temperatura_display_bits[7]), .b(controller_1_temperatura_display_bits[8]),
    .e(controller_1_temperatura_display_bits[11]), .d(controller_1_temperatura_display_bits[9]),
    .c(controller_1_temperatura_display_bits[10]));  // open: dp
  _7_Segment_Display u_7_segment_display_2 (
    .g(controller_1_temperatura_display_bits[4]), .f(controller_1_temperatura_display_bits[3]),
    .a(controller_1_temperatura_display_bits[2]), .b(controller_1_temperatura_display_bits[1]),
    .d(controller_1_temperatura_display_bits[6]), .c(controller_1_temperatura_display_bits[5]),
    .dp(controller_1_temperatura_display_bits[0]));  // open: e
endmodule

module BCD_to_7_segmented_decoder (
  input  D,
  input  C,
  input  B,
  input  A,
  output a_2,
  output b_2,
  output c_2,
  output d_2,
  output e,
  output f,
  output g
);

  wire and_1_out, and_2_out, and_3_out, and_4_out, and_5_out, and_6_out, and_7_out, and_8_out, and_9_out,
       and_10_out, and_11_out, and_12_out, and_13_out, and_14_out, and_15_out, and_16_out, not_1_out,
       not_2_out, not_3_out, not_4_out, not_5_out, not_6_out, not_7_out, not_8_out, not_9_out, not_10_out,
       not_11_out, not_12_out, not_13_out, not_14_out, not_15_out, not_16_out, not_17_out, not_18_out,
       not_19_out, not_20_out, not_21_out;

  not not_1 (not_1_out, C);
  and and_1 (and_1_out, not_1_out, not_2_out);
  not not_2 (not_2_out, A);
  and and_2 (and_2_out, C, A);
  not not_3 (not_3_out, C);
  not not_4 (not_4_out, B);
  and and_3 (and_3_out, not_4_out, not_5_out);
  not not_5 (not_5_out, A);
  and and_4 (and_4_out, B, A);
  not not_6 (not_6_out, B);
  or or_1 (c_2, not_6_out, A, C);
  not not_7 (not_7_out, C);
  and and_5 (and_5_out, not_7_out, not_8_out);
  not not_8 (not_8_out, A);
  not not_9 (not_9_out, C);
  and and_6 (and_6_out, not_9_out, B);
  and and_7 (and_7_out, B, not_10_out);
  not not_10 (not_10_out, A);
  and and_8 (and_8_out, C, not_11_out, A);
  not not_11 (not_11_out, B);
  not not_12 (not_12_out, C);
  and and_9 (and_9_out, not_12_out, not_13_out);
  not not_13 (not_13_out, A);
  and and_10 (and_10_out, B, not_14_out);
  not not_14 (not_14_out, A);
  not not_15 (not_15_out, B);
  and and_11 (and_11_out, not_15_out, not_16_out);
  not not_16 (not_16_out, A);
  and and_12 (and_12_out, C, not_17_out);
  not not_17 (not_17_out, B);
  and and_13 (and_13_out, C, not_18_out);
  not not_18 (not_18_out, A);
  not not_19 (not_19_out, C);
  and and_14 (and_14_out, not_19_out, B);
  and and_15 (and_15_out, C, not_20_out);
  not not_20 (not_20_out, B);
  and and_16 (and_16_out, C, not_21_out);
  not not_21 (not_21_out, A);
  or or_2 (a_2, and_1_out, B, and_2_out, D);
  or or_3 (b_2, not_3_out, and_3_out, and_4_out);
  or or_4 (d_2, and_5_out, and_6_out, and_7_out, and_8_out, D);
  or or_5 (e, and_9_out, and_10_out);
  or or_6 (f, and_11_out, and_12_out, and_13_out, D);
  or or_7 (g, and_14_out, and_15_out, and_16_out, D);
endmodule

// Dp M
module DisplayManager (
  input  [4:0] T_opt,
  input  [4:0] T_opt_2,
  input  Reset,
  input  Reset_2,
  input  [4:0] T_opt_3,
  output [4:0] out_6,
  output [4:0] out_7,
  output [4:0] out_8,
  output [3:0] enice,
  output [3:0] desetice
);

  wire bcd_to_7_segmented_decoder_1_a_2, bcd_to_7_segmented_decoder_1_b_2, bcd_to_7_segmented_decoder_1_c_2,
       bcd_to_7_segmented_decoder_1_d_2, bcd_to_7_segmented_decoder_1_e, bcd_to_7_segmented_decoder_1_f,
       bcd_to_7_segmented_decoder_1_g, bcd_to_7_segmented_decoder_2_a_2, bcd_to_7_segmented_decoder_2_b_2,
       bcd_to_7_segmented_decoder_2_c_2, bcd_to_7_segmented_decoder_2_d_2, bcd_to_7_segmented_decoder_2_e,
       bcd_to_7_segmented_decoder_2_f, bcd_to_7_segmented_decoder_2_g, clock_1_out,
       n5_bit_shifter_left_2_overflow, n5_bit_shifter_left_3_overflow;
  wire [3:0] adder_2_cout, n5_bit_shifter_left_1_overflow;
  wire [4:0] adder_1_out, n5_bit_shifter_left_1_shifted_bits, n5_bit_shifter_left_2_shifted_bits,
       n5_bit_shifter_left_3_shifted_bits, shifter_1_out, shifter_2_out;

  Clock clock_1 (.out(clock_1_out));
  Shifter #(.width(5)) shifter_1 (.in(T_opt_3), .\dist (3'b011), .out(shifter_1_out));
  Register #(.width(5)) u_Desetice (.D(T_opt), .Q(out_6), .clk(clock_1_out), .clr(Reset));  // open: en
  Adder #(.width(5)) adder_1 (.a(shifter_1_out), .b(5'b00011), .out(adder_1_out));  // open: cin, cout
  Register #(.width(5)) binary (.D(out_6), .Q(out_7), .clk(clock_1_out), .clr(Reset));  // open: en
  Shifter #(.width(5)) shifter_2 (.in(adder_1_out), .\dist (3'b001), .out(shifter_2_out));
  Register #(.width(5)) u_Enice (.D(out_7), .Q(out_8), .clk(clock_1_out), .clr(Reset));  // open: en
  BCD_to_7_segmented_decoder bcd_to_7_segmented_decoder_1 (
    .D(adder_1_out[1]), .C(adder_1_out[2]), .B(adder_1_out[3]), .A(adder_1_out[4]),
    .a_2(bcd_to_7_segmented_decoder_1_a_2), .b_2(bcd_to_7_segmented_decoder_1_b_2),
    .c_2(bcd_to_7_segmented_decoder_1_c_2), .d_2(bcd_to_7_segmented_decoder_1_d_2),
    .e(bcd_to_7_segmented_decoder_1_e), .f(bcd_to_7_segmented_decoder_1_f), .g(bcd_to_7_segmented_decoder_1_g));
  BCD_to_7_segmented_decoder bcd_to_7_segmented_decoder_2 (
    .D(shifter_2_out[1]), .C(shifter_2_out[2]), .B(shifter_2_out[3]), .A(shifter_2_out[4]),
    .a_2(bcd_to_7_segmented_decoder_2_a_2), .b_2(bcd_to_7_segmented_decoder_2_b_2),
    .c_2(bcd_to_7_segmented_decoder_2_c_2), .d_2(bcd_to_7_segmented_decoder_2_d_2),
    .e(bcd_to_7_segmented_decoder_2_e), .f(bcd_to_7_segmented_decoder_2_f), .g(bcd_to_7_segmented_decoder_2_g));
  _7_Segment_Display u_7_segment_display_1 (
    .g(bcd_to_7_segmented_decoder_1_g), .f(bcd_to_7_segmented_decoder_1_f),
    .a(bcd_to_7_segmented_decoder_1_a_2), .b(bcd_to_7_segmented_decoder_1_b_2),
    .e(bcd_to_7_segmented_decoder_1_e), .d(bcd_to_7_segmented_decoder_1_d_2),
    .c(bcd_to_7_segmented_decoder_1_c_2));  // open: dp
  _7_Segment_Display u_7_segment_display_2 (
    .g(bcd_to_7_segmented_decoder_2_g), .f(bcd_to_7_segmented_decoder_2_f),
    .a(bcd_to_7_segmented_decoder_2_a_2), .b(bcd_to_7_segmented_decoder_2_b_2),
    .e(bcd_to_7_segmented_decoder_2_e), .d(bcd_to_7_segmented_decoder_2_d_2),
    .c(bcd_to_7_segmented_decoder_2_c_2));  // open: dp
  _5_bit_shifter_left u_5_bit_shifter_left_1 (
    .in_1(T_opt_2), .shifted_bits(n5_bit_shifter_left_1_shifted_bits),
    .overflow(n5_bit_shifter_left_1_overflow[0]));
  _5_bit_shifter_left u_5_bit_shifter_left_2 (
    .in_1(n5_bit_shifter_left_3_shifted_bits), .shifted_bits(n5_bit_shifter_left_2_shifted_bits),
    .overflow(n5_bit_shifter_left_2_overflow));
  _5_bit_shifter_left u_5_bit_shifter_left_3 (
    .in_1(n5_bit_shifter_left_1_shifted_bits), .shifted_bits(n5_bit_shifter_left_3_shifted_bits),
    .overflow(n5_bit_shifter_left_3_overflow));
  Comparator #(.width(5), .mode("unsigned")) comparator_1 (
    .a(n5_bit_shifter_left_2_shifted_bits), .b(5'b00100));  // open: gt, eq, lt
  Adder #(.width(4)) adder_2 (
    .a(n5_bit_shifter_left_2_shifted_bits[4:1]), .b(4'b0011), .out(enice), .cout(adder_2_cout[0]));  // open: cin
  Adder #(.width(4)) adder_3 (.a(n5_bit_shifter_left_1_overflow), .b(adder_2_cout), .out(desetice));  // open: cin, cout
endmodule

// CTR
module Controller (
  input  [4:0] T_opt,
  input  [7:0] Temperatura,
  input  [3:0] Pritisk,
  input  [3:0] Vlaga,
  input  Reset,
  output [13:0] temperatura_display_bits,
  output [3:0] K_ogrevanje,
  output [3:0] K_okno
);

  DisplayManager displaymanager_1 (.T_opt(T_opt));  // open: T_opt_2, Reset, Reset_2, T_opt_3, out_6, out_7, out_8, enice, desetice
endmodule

// SL5
module _5_bit_shifter_left (
  input  [4:0] in_1,
  output [4:0] shifted_bits,
  output overflow
);


  assign overflow = in_1[4];
  assign shifted_bits = {in_1[3:0], 1'b0};
endmodule
