// Logisim project 10_recreatedTable_adding_allSameStates.circ as structural Verilog: 6 circuits, main circuit 1
module _1 (
);

  wire \_5_stanjski_števec_carry , and_1_out, and_2_out, and_3_out, Clk_out, comparator_1_eq,
       comparator_1_gt, comparator_1_lt, Hranjenje_Err_vrednosti_do_nove_akcije_q,
       Hranjenje_trenutne_akcije_q, Hranjenje_zamenjana_vrednosti_do_nove_akcije_q, keyboard_1_avail,
       not_1_out, not_2_out, Odkleni_out, or_1_out, or_2_out, or_3_out, or_4_out, or_5_out, register_1_q,
       register_2_q, register_3_q, \Vpiši_out , Z_out, Zamik_napake___Reset_q;
  wire [2:0] \_5_stanjski_števec_q ;
  wire [3:0] ram_1_data;
  wire [6:0] keyboard_1_data;

  Clock Clk (.out(Clk_out));
  Button \Vpiši  (.out(\Vpiši_out ));
  Button Odkleni (.out(Odkleni_out));
  Button Z (.out(Z_out));
  not not_1 (not_1_out, \Vpiši_out );
  or or_1 (or_1_out, \Vpiši_out , Odkleni_out);
  Register #(.width(1)) Hranjenje_trenutne_akcije (
    .D(not_1_out), .Q(Hranjenje_trenutne_akcije_q), .clk(or_1_out), .clr(or_5_out));  // open: en
  Register #(.width(1)) register_1 (.D(Z_out), .Q(register_1_q), .clk(Z_out), .clr(or_5_out));  // open: en
  or or_2 (or_2_out, or_1_out, Z_out);
  Register #(.width(1)) register_2 (.D(or_1_out), .Q(register_2_q), .clk(or_1_out), .clr(or_5_out));  // open: en
  and and_1 (and_1_out, keyboard_1_avail, Clk_out, register_2_q);
  Comparator #(.width(4)) comparator_1 (
    .a(keyboard_1_data[3:0]), .b(ram_1_data), .gt(comparator_1_gt), .eq(comparator_1_eq), .lt(comparator_1_lt));
  or or_3 (or_3_out, comparator_1_lt, comparator_1_gt);
  Keyboard #(.buflen(4)) keyboard_1 (
    .clk(and_1_out), .clr(or_5_out), .avail(keyboard_1_avail), .data(keyboard_1_data));  // open: re
  Counter #(.width(3), .max('h4)) \_5_stanjski_števec  (
    .load(1'b0), .count(comparator_1_eq), .Q(\_5_stanjski_števec_q ), .carry(\_5_stanjski_števec_carry ),
    .clk(and_1_out), .clr(or_5_out));  // open: D
  and and_2 (and_2_out, keyboard_1_avail, or_3_out, Hranjenje_trenutne_akcije_q);
  or or_4 (or_4_out, and_2_out, register_1_q);
  RAM #(.addrWidth(2), .dataWidth(4)) ram_1 (
    .addr(\_5_stanjski_števec_q [1:0]), .data(ram_1_data), .sel(1'b1), .clk(and_1_out),
    .ld(Hranjenje_trenutne_akcije_q));  // open: clr
  not not_2 (not_2_out, Hranjenje_trenutne_akcije_q);
  D_Flip_Flop Zamik_napake___Reset (
    .clk(Clk_out), .D(or_4_out), .Q(Zamik_napake___Reset_q), .en(1'b1));  // open: Qn, preset, reset
  assign ram_1_data = not_2_out ? keyboard_1_data[3:0] : 4'bz;  // Controlled_Buffer controlled_buffer_1
  or or_5 (or_5_out, Zamik_napake___Reset_q, \_5_stanjski_števec_carry );
  Register #(.width(1)) register_3 (
    .D(\_5_stanjski_števec_carry ), .Q(register_3_q), .clk(\_5_stanjski_števec_carry ),
    .clr(Zamik_napake___Reset_q));  // open: en
  and and_3 (and_3_out, not_2_out, \_5_stanjski_števec_carry , register_3_q);
  Register #(.width(1)) Hranjenje_zamenjana_vrednosti_do_nove_akcije (
    .D(and_3_out), .Q(Hranjenje_zamenjana_vrednosti_do_nove_akcije_q), .clk(and_3_out), .clr(or_2_out));  // open: en
  Register #(.width(1)) Hranjenje_Err_vrednosti_do_nove_akcije (
    .D(Zamik_napake___Reset_q), .Q(Hranjenje_Err_vrednosti_do_nove_akcije_q), .clk(Zamik_napake___Reset_q),
    .clr(or_2_out));  // open: en
  LED K_veljavna (.in(Hranjenje_zamenjana_vrednosti_do_nove_akcije_q));
  LED O_Z (.in(register_3_q));
  LED Err (.in(Hranjenje_Err_vrednosti_do_nove_akcije_q));

  // Notes on the sheet:
  //   Ura - ko niz v tipkovnici in trenutno akcija in urina perioda
  //   Operacija Zakleni - resetira vezje
  //   Resetiranje ob novi akciji
  //   Operacija Vpis ali Odkleni
  //   Comparator
  //   Tipkovnica
  //   Potrebujemo 2 bita za naslov
  //   Preverjanje ali je res prišlo do napake
  //   4x4 RAM
  //   3 stanjski kontroler
  //   Hranjenje odklenjena vrednosti
  //   Resetiranje ob prehodu stanja nazaj - konec vpisa, odklenjena ključavnica ali err
  //   Potrebujemo le 4 bite
  //   Preverjanje ali smo res vpisali nov niz
endmodule

module stevec (
  input  [6:0] Keyboard,
  input  Clk,
  input  Akcija__read_write,
  input  Reset,
  output OK,
  output Err
);

  wire comparator_1_eq, comparator_1_gt, comparator_1_lt, not_1_out;
  wire [2:0] \_5_stanjski_števec_q ;
  wire [3:0] ram_1_data;

  RAM #(.addrWidth(2), .dataWidth(4)) ram_1 (
    .addr(\_5_stanjski_števec_q [1:0]), .data(ram_1_data), .sel(1'b1), .clk(Clk), .ld(Akcija__read_write));  // open: clr
  not not_1 (not_1_out, Akcija__read_write);
  assign ram_1_data = not_1_out ? Keyboard[3:0] : 4'bz;  // Controlled_Buffer controlled_buffer_1
  Comparator #(.width(4)) comparator_1 (
    .a(Keyboard[3:0]), .b(ram_1_data), .gt(comparator_1_gt), .eq(comparator_1_eq), .lt(comparator_1_lt));
  or or_1 (Err, comparator_1_lt, comparator_1_gt);
  Counter #(.width(3), .max('h4)) \_5_stanjski_števec  (
    .load(1'b0), .count(comparator_1_eq), .Q(\_5_stanjski_števec_q ), .carry(OK), .clk(Clk), .clr(Reset));  // open: D

  // Notes on the sheet:
  //   Potrebujemo le 4 bite
  //   4x4 RAM
  //   3 stanjski kontroler
  //   Comparator
endmodule

module finishedPrehanjanja (
  input  VPIS,
  input  ODKLENI,
  input  ZAKLENI,
  input  NAPREJ,
  input  ERR,
  input  S2,
  input  S1,
  input  S0,
  output S2_2,
  output S1_2,
  output S0_2
);

  wire and_1_out, and_2_out, and_3_out, and_4_out, and_5_out, and_6_out, and_7_out, not_1_out, not_2_out,
       not_3_out, not_4_out, not_5_out, not_6_out, not_7_out, not_8_out, not_9_out, not_10_out, not_11_out;

  not not_1 (not_1_out, ZAKLENI);
  and and_1 (and_1_out, not_1_out, S2, not_2_out);
  not not_2 (not_2_out, S0);
  and and_2 (and_2_out, NAPREJ, not_3_out);
  not not_3 (not_3_out, S1);
  not not_4 (not_4_out, ZAKLENI);
  and and_3 (and_3_out, not_4_out, not_5_out, not_6_out);
  not not_5 (not_5_out, S2);
  not not_6 (not_6_out, S0);
  and and_4 (and_4_out, ODKLENI, S0);
  not not_7 (not_7_out, ODKLENI);
  and and_5 (and_5_out, not_7_out, not_8_out);
  not not_8 (not_8_out, ZAKLENI);
  not not_9 (not_9_out, ZAKLENI);
  and and_6 (and_6_out, not_9_out, S1);
  not not_10 (not_10_out, ZAKLENI);
  and and_7 (and_7_out, not_10_out, S2, not_11_out);
  not not_11 (not_11_out, S0);
  or or_1 (S2_2, and_1_out, and_2_out);
  or or_2 (S1_2, and_3_out, and_4_out);
  or or_3 (S0_2, and_5_out, and_6_out, and_7_out);
endmodule

module ImplementingPrehajanjaNStevec (
  input  Vpis,
  input  Odkleni,
  input  Zakleni,
  input  ReadWrite____0_Write
);

  wire clock_1_out, fixedprehajanjestanj_1_s0_2, fixedprehajanjestanj_1_s1_2, fixedprehajanjestanj_1_s2_2,
       lucicircuit_1_err, lucicircuit_1_odklenjeno, lucicircuit_1_vpisano, Reset_out, S0_q, S1_q, S2_q,
       stevec_1_err, stevec_1_ok;
  wire [6:0] keyboard_1_data;

  Clock clock_1 (.out(clock_1_out));
  Keyboard #(.buflen(4)) keyboard_1 (.clk(clock_1_out), .data(keyboard_1_data));  // open: re, clr, avail
  stevec stevec_1 (
    .Keyboard(keyboard_1_data), .Clk(clock_1_out), .Akcija__read_write(ReadWrite____0_Write),
    .Reset(Reset_out), .OK(stevec_1_ok), .Err(stevec_1_err));
  fixedPrehajanjeStanj fixedprehajanjestanj_1 (
    .VPIS(Vpis), .ODKLENI(Odkleni), .ZAKLENI(Zakleni), .NAPREJ(stevec_1_ok), .ERR(stevec_1_err), .S2(S2_q),
    .S1(S1_q), .S0(S0_q), .S2_2(fixedprehajanjestanj_1_s2_2), .S1_2(fixedprehajanjestanj_1_s1_2),
    .S0_2(fixedprehajanjestanj_1_s0_2));
  LED Odklenjeno (.in(lucicircuit_1_odklenjeno));
  luciCircuit lucicircuit_1 (
    .S2(fixedprehajanjestanj_1_s2_2), .S1(fixedprehajanjestanj_1_s1_2), .S0(fixedprehajanjestanj_1_s0_2),
    .ODKLENJENO(lucicircuit_1_odklenjeno), .VPISANO(lucicircuit_1_vpisano), .ERR(lucicircuit_1_err));
  LED Vpisano (.in(lucicircuit_1_vpisano));
  LED Error (.in(lucicircuit_1_err));
  D_Flip_Flop S2 (
    .clk(clock_1_out), .D(fixedprehajanjestanj_1_s2_2), .Q(S2_q), .en(1'b1), .reset(Reset_out));  // open: Qn, preset
  D_Flip_Flop S1 (
    .clk(clock_1_out), .D(fixedprehajanjestanj_1_s1_2), .Q(S1_q), .en(1'b1), .reset(Reset_out));  // open: Qn, preset
  D_Flip_Flop S0 (
    .clk(clock_1_out), .D(fixedprehajanjestanj_1_s0_2), .Q(S0_q), .en(1'b1), .reset(Reset_out));  // open: Qn, preset
  Button Reset (.out(Reset_out));
endmodule

module luciCircuit (
  input  S2,
  input  S1,
  input  S0,
  output ODKLENJENO,
  output VPISANO,
  output ERR
);

  wire and_2_out, and_3_out, not_1_out, not_2_out, not_3_out;

  not not_1 (not_1_out, S2);
  not not_2 (not_2_out, S0);
  not not_3 (not_3_out, S0);
  and and_1 (ERR, S2, S0);
  and and_2 (and_2_out, not_1_out, S0);
  and and_3 (and_3_out, S2, not_2_out);
  and and_4 (VPISANO, S2, not_3_out);
  or or_1 (ODKLENJENO, and_2_out, and_3_out);
endmodule

module fixedPrehajanjeStanj (
  input  VPIS,
  input  ODKLENI,
  input  ZAKLENI,
  input  NAPREJ,
  input  ERR,
  input  S2,
  input  S1,
  input  S0,
  output S2_2,
  output S1_2,
  output S0_2
);

  wire and_1_out, and_2_out, and_3_out, and_4_out, and_5_out, and_6_out, and_7_out, and_8_out, not_1_out,
       not_2_out, not_3_out, not_4_out, not_5_out, not_6_out, not_7_out, not_8_out, not_9_out, not_10_out,
       not_11_out;

  not not_1 (not_1_out, ODKLENI);
  not not_2 (not_2_out, ZAKLENI);
  and and_1 (and_1_out, not_1_out, not_2_out, S2);
  not not_3 (not_3_out, ZAKLENI);
  and and_2 (and_2_out, not_3_out, S2, not_4_out);
  not not_4 (not_4_out, S0);
  and and_3 (and_3_out, NAPREJ, not_5_out);
  not not_5 (not_5_out, S1);
  not not_6 (not_6_out, VPIS);
  not not_7 (not_7_out, ZAKLENI);
  not not_8 (not_8_out, ERR);
  not not_9 (not_9_out, S2);
  not not_10 (not_10_out, ODKLENI);
  and and_4 (and_4_out, not_10_out, not_11_out, S0);
  not not_11 (not_11_out, ZAKLENI);
  and and_5 (and_5_out, ODKLENI, S1);
  or or_1 (S2_2, and_1_out, and_2_out, ERR, and_3_out);
  and and_6 (and_6_out, not_6_out, not_7_out, not_8_out, S1);
  or or_2 (S1_2, and_6_out, and_7_out, and_8_out);
  and and_7 (and_7_out, ODKLENI, not_9_out);
  and and_8 (and_8_out, ODKLENI, S0);
  or or_3 (S0_2, and_4_out, ERR, NAPREJ, and_5_out);
endmodule
