// Logisim project 14_odklepanje_koda_ontoError.circ as structural Verilog: 8 circuits, main circuit 1
module _1 (
);

  wire \_5_stanjski_števec_carry , and_1_out, and_2_out, and_3_out, Clk_out, comparator_1_eq,
       comparator_1_gt, comparator_1_lt, Hranjenje_Err_vrednosti_do_nove_akcije_q,
       Hranjenje_trenutne_akcije_q, Hranjenje_zamenjana_vrednosti_do_nove_akcije_q, keyboard_1_avail,
       not_1_out, not_2_out, Odkleni_out, or_1_out, or_2_out, or_3_out, or_4_out, or_5_out, register_1_q,
       register_2_q, register_3_q, \Vpiši_out , Z_out, Zamik_napake___Reset_q;
  wire [2:0] \_5_stanjski_števec_q ;
  wire [3:0] ram_1_data;
  wire [6:0] keyboard_1_data;

  Clock Clk (.out(Clk_out));
  Button \Vpiši  (.out(\Vpiši_out ));
  Button Odkleni (.out(Odkleni_out));
  Button Z (.out(Z_out));
  not not_1 (not_1_out, \Vpiši_out );
  or or_1 (or_1_out, \Vpiši_out , Odkleni_out);
  Register #(.width(1)) Hranjenje_trenutne_akcije (
    .D(not_1_out), .Q(Hranjenje_trenutne_akcije_q), .clk(or_1_out), .clr(or_5_out));  // open: en
  Register #(.width(1)) register_1 (.D(Z_out), .Q(register_1_q), .clk(Z_out), .clr(or_5_out));  // open: en
  or or_2 (or_2_out, or_1_out, Z_out);
  Register #(.width(1)) register_2 (.D(or_1_out), .Q(register_2_q), .clk(or_1_out), .clr(or_5_out));  // open: en
  and and_1 (and_1_out, keyboard_1_avail, Clk_out, register_2_q);
  Comparator #(.width(4)) comparator_1 (
    .a(keyboard_1_data[3:0]), .b(ram_1_data), .gt(comparator_1_gt), .eq(comparator_1_eq), .lt(comparator_1_lt));
  or or_3 (or_3_out, comparator_1_lt, comparator_1_gt);
  Keyboard #(.buflen(4)) keyboard_1 (
    .clk(and_1_out), .clr(or_5_out), .avail(keyboard_1_avail), .data(keyboard_1_data));  // open: re
  Counter #(.width(3), .max('h4)) \_5_stanjski_števec  (
    .load(1'b0), .count(comparator_1_eq), .Q(\_5_stanjski_števec_q ), .carry(\_5_stanjski_števec_carry ),
    .clk(and_1_out), .clr(or_5_out));  // open: D
  and and_2 (and_2_out, keyboard_1_avail, or_3_out, Hranjenje_trenutne_akcije_q);
  or or_4 (or_4_out, and_2_out, register_1_q);
  RAM #(.addrWidth(2), .dataWidth(4)) ram_1 (
    .addr(\_5_stanjski_števec_q [1:0]), .data(ram_1_data), .sel(1'b1), .clk(and_1_out),
    .ld(Hranjenje_trenutne_akcije_q));  // open: clr
  not not_2 (not_2_out, Hranjenje_trenutne_akcije_q);
  D_Flip_Flop Zamik_napake___Reset (
    .clk(Clk_out), .D(or_4_out), .Q(Zamik_napake___Reset_q), .en(1'b1));  // open: Qn, preset, reset
  assign ram_1_data = not_2_out ? keyboard_1_data[3:0] : 4'bz;  // Controlled_Buffer controlled_buffer_1
  or or_5 (or_5_out, Zamik_napake___Reset_q, \_5_stanjski_števec_carry );
  Register #(.width(1)) register_3 (
    .D(\_5_stanjski_števec_carry ), .Q(register_3_q), .clk(\_5_stanjski_števec_carry ),
    .clr(Zamik_napake___Reset_q));  // open: en
  and and_3 (and_3_out, not_2_out, \_5_stanjski_števec_carry , register_3_q);
  Register #(.width(1)) Hranjenje_zamenjana_vrednosti_do_nove_akcije (
    .D(and_3_out), .Q(Hranjenje_zamenjana_vrednosti_do_nove_akcije_q), .clk(and_3_out), .clr(or_2_out));  // open: en
  Register #(.width(1)) Hranjenje_Err_vrednosti_do_nove_akcije (
    .D(Zamik_napake___Reset_q), .Q(Hranjenje_Err_vrednosti_do_nove_akcije_q), .clk(Zamik_napake___Reset_q),
    .clr(or_2_out));  // open: en
  LED K_veljavna (.in(Hranjenje_zamenjana_vrednosti_do_nove_akcije_q));
  LED O_Z (.in(register_3_q));
  LED Err (.in(Hranjenje_Err_vrednosti_do_nove_akcije_q));

  // Notes on the sheet:
  //   Ura - ko niz v tipkovnici in trenutno akcija in urina perioda
  //   Operacija Zakleni - resetira vezje
  //   Resetiranje ob novi akciji
  //   Operacija Vpis ali Odkleni
  //   Comparator
  //   Tipkovnica
  //   Potrebujemo 2 bita za naslov
  //   Preverjanje ali je res prišlo do napake
  //   4x4 RAM
  //   3 stanjski kontroler
  //   Hranjenje odklenjena vrednosti
  //   Resetiranje ob prehodu stanja nazaj - konec vpisa, odklenjena ključavnica ali err
  //   Potrebujemo le 4 bite
  //   Preverjanje ali smo res vpisali nov niz
endmodule

module stevec (
  input  IsInput,
  input  [6:0] Keyboard,
  input  Clk,
  input  Akcija__read_write,
  input  Reset,
  input  NormalClock,
  output [2:0] STATE_TEMP,
  output OK,
  output Err
);

  wire comparator_1_eq, comparator_1_gt, comparator_1_lt, not_1_out, or_1_out, or_2_out,
       Zamik_napake___Reset_q;
  wire [3:0] ram_1_data;

  RAM #(.addrWidth(2), .dataWidth(4)) ram_1 (
    .addr(STATE_TEMP[1:0]), .data(ram_1_data), .sel(1'b1), .clk(Clk), .ld(Akcija__read_write));  // open: clr
  not not_1 (not_1_out, Akcija__read_write);
  assign ram_1_data = not_1_out ? Keyboard[3:0] : 4'bz;  // Controlled_Buffer controlled_buffer_1
  Comparator #(.width(4)) comparator_1 (
    .a(Keyboard[3:0]), .b(ram_1_data), .gt(comparator_1_gt), .eq(comparator_1_eq), .lt(comparator_1_lt));
  or or_1 (or_1_out, comparator_1_lt, comparator_1_gt);
  Counter #(.width(3), .max('h4)) \_5_stanjski_števec  (
    .load(1'b0), .count(comparator_1_eq), .Q(STATE_TEMP), .carry(OK), .clk(Clk), .clr(or_2_out));  // open: D
  or or_2 (or_2_out, Reset, Zamik_napake___Reset_q);
  D_Flip_Flop Zamik_napake___Reset (
    .clk(NormalClock), .D(OK), .Q(Zamik_napake___Reset_q), .en(1'b1));  // open: Qn, preset, reset

  assign Err = 1'b0;

  // Notes on the sheet:
  //   Potrebujemo le 4 bite
  //   4x4 RAM
  //   3 stanjski kontroler
  //   Comparator
endmodule

module finishedPrehanjanja (
  input  VPIS,
  input  ODKLENI,
  input  ZAKLENI,
  input  NAPREJ,
  input  ERR,
  input  S2,
  input  S1,
  input  S0,
  output S2_2,
  output S1_2,
  output S0_2
);

  wire and_1_out, and_2_out, and_3_out, and_4_out, and_5_out, and_6_out, and_7_out, not_1_out, not_2_out,
       not_3_out, not_4_out, not_5_out, not_6_out, not_7_out, not_8_out, not_9_out, not_10_out, not_11_out;

  not not_1 (not_1_out, ZAKLENI);
  and and_1 (and_1_out, not_1_out, S2, not_2_out);
  not not_2 (not_2_out, S0);
  and and_2 (and_2_out, NAPREJ, not_3_out);
  not not_3 (not_3_out, S1);
  not not_4 (not_4_out, ZAKLENI);
  not not_5 (not_5_out, S2);
  and and_3 (and_3_out, not_4_out, not_5_out, not_6_out);
  not not_6 (not_6_out, S0);
  and and_4 (and_4_out, ODKLENI, S0);
  not not_7 (not_7_out, ODKLENI);
  and and_5 (and_5_out, not_7_out, not_8_out);
  not not_8 (not_8_out, ZAKLENI);
  not not_9 (not_9_out, ZAKLENI);
  and and_6 (and_6_out, not_9_out, S1);
  not not_10 (not_10_out, ZAKLENI);
  and and_7 (and_7_out, not_10_out, S2, not_11_out);
  not not_11 (not_11_out, S0);
  or or_1 (S2_2, and_1_out, and_2_out);
  or or_2 (S1_2, and_3_out, and_4_out);
  or or_3 (S0_2, and_5_out, and_6_out, and_7_out);
endmodule

module ImplementingPrehajanjaNStevec (
  output [2:0] out_1
);

  wire alloutputsfixed_1_s02, alloutputsfixed_1_s12, alloutputsfixed_1_s22, and_1_out, clock_1_out,
       Hranjenje_trenutne_akcije_read_write_2_q, Hranjenje_trenutne_akcije_read_write_q, keyboard_1_avail,
       lucicircuit_1_err, lucicircuit_1_odklenjeno, lucicircuit_1_vpisano, New_CLOCK_out, not_1_out,
       not_2_out, not_3_out, Odkleni_out, or_1_out, or_2_out, or_3_out, register_1_q, Reset_out, S0_q, S1_q,
       S2_q, stevec_1_err, stevec_1_ok, \Vpiši_out , Z_out;
  wire [6:0] keyboard_1_data;

  Button \Vpiši  (.out(\Vpiši_out ));
  Button Odkleni (.out(Odkleni_out));
  Button Z (.out(Z_out));
  not not_1 (not_1_out, \Vpiši_out );
  or or_1 (or_1_out, \Vpiši_out , Odkleni_out);
  Register #(.width(1)) Hranjenje_trenutne_akcije_read_write (
    .D(Z_out), .Q(Hranjenje_trenutne_akcije_read_write_q), .clk(Z_out));  // open: en, clr
  Register #(.width(1)) Hranjenje_trenutne_akcije_read_write_2 (
    .D(not_1_out), .Q(Hranjenje_trenutne_akcije_read_write_2_q), .clk(or_1_out), .clr(or_3_out));  // open: en
  Register #(.width(1)) register_1 (.D(or_1_out), .Q(register_1_q), .clk(or_1_out), .clr(or_3_out));  // open: en
  Clock clock_1 (.out(clock_1_out));
  and New_CLOCK (New_CLOCK_out, register_1_q, clock_1_out);
  Keyboard #(.buflen(4)) keyboard_1 (
    .clk(New_CLOCK_out), .clr(or_3_out), .avail(keyboard_1_avail), .data(keyboard_1_data));  // open: re
  not not_2 (not_2_out, Hranjenje_trenutne_akcije_read_write_2_q);
  not not_3 (not_3_out, Hranjenje_trenutne_akcije_read_write_q);
  stevec stevec_1 (
    .IsInput(keyboard_1_avail), .Keyboard(keyboard_1_data), .Clk(New_CLOCK_out),
    .Akcija__read_write(Hranjenje_trenutne_akcije_read_write_2_q), .Reset(Reset_out),
    .NormalClock(clock_1_out), .STATE_TEMP(out_1), .OK(stevec_1_ok), .Err(stevec_1_err));
  or or_2 (or_2_out, stevec_1_ok, stevec_1_err);
  and and_1 (and_1_out, not_2_out, register_1_q, not_3_out);
  ALLOUTPUTSFIXED alloutputsfixed_1 (
    .VPIS(and_1_out), .ODKLENI(Hranjenje_trenutne_akcije_read_write_2_q),
    .ZAKLENI(Hranjenje_trenutne_akcije_read_write_q), .NAPREJ(stevec_1_ok), .ERR(stevec_1_err), .S2(S2_q),
    .S1(S1_q), .S0(S0_q), .S22(alloutputsfixed_1_s22), .S12(alloutputsfixed_1_s12),
    .S02(alloutputsfixed_1_s02));
  luciCircuit lucicircuit_1 (
    .S2(alloutputsfixed_1_s22), .S1(alloutputsfixed_1_s12), .S0(alloutputsfixed_1_s02),
    .ODKLENJENO(lucicircuit_1_odklenjeno), .VPISANO(lucicircuit_1_vpisano), .ERR(lucicircuit_1_err));
  D_Flip_Flop S2 (
    .clk(clock_1_out), .D(alloutputsfixed_1_s22), .Q(S2_q), .en(1'b1), .reset(Reset_out));  // open: Qn, preset
  D_Flip_Flop S1 (
    .clk(clock_1_out), .D(alloutputsfixed_1_s12), .Q(S1_q), .en(1'b1), .reset(Reset_out));  // open: Qn, preset
  D_Flip_Flop S0 (
    .clk(clock_1_out), .D(alloutputsfixed_1_s02), .Q(S0_q), .en(1'b1), .reset(Reset_out));  // open: Qn, preset
  or or_3 (or_3_out, or_2_out, Reset_out);
  Button Reset (.out(Reset_out));
  LED Odklenjeno (.in(lucicircuit_1_odklenjeno));
  LED Vpisano (.in(lucicircuit_1_vpisano));
  LED Error (.in(lucicircuit_1_err));
endmodule

module luciCircuit (
  input  S2,
  input  S1,
  input  S0,
  output ODKLENJENO,
  output VPISANO,
  output ERR
);

  wire and_2_out, and_3_out, not_1_out, not_2_out, not_3_out;

  not not_1 (not_1_out, S2);
  not not_2 (not_2_out, S0);
  not not_3 (not_3_out, S0);
  and and_1 (ERR, S2, S0);
  and and_2 (and_2_out, not_1_out, S0);
  and and_3 (and_3_out, S2, not_2_out);
  and and_4 (VPISANO, S2, not_3_out);
  or or_1 (ODKLENJENO, and_2_out, and_3_out);
endmodule

module fixedPrehajanjeStanj (
  input  VPIS,
  input  ODKLENI,
  input  ZAKLENI,
  input  NAPREJ,
  input  ERR,
  input  S2,
  input  S1,
  input  S0,
  output S2_2,
  output S1_2,
  output S0_2
);

  wire and_1_out, and_2_out, and_3_out, and_4_out, and_5_out, and_6_out, and_7_out, and_8_out, not_1_out,
       not_2_out, not_3_out, not_4_out, not_5_out, not_6_out, not_7_out, not_8_out, not_9_out, not_10_out,
       not_11_out;

  not not_1 (not_1_out, ODKLENI);
  not not_2 (not_2_out, ZAKLENI);
  and and_1 (and_1_out, not_1_out, not_2_out, S2);
  not not_3 (not_3_out, ZAKLENI);
  and and_2 (and_2_out, not_3_out, S2, not_4_out);
  not not_4 (not_4_out, S0);
  and and_3 (and_3_out, NAPREJ, not_5_out);
  not not_5 (not_5_out, S1);
  not not_6 (not_6_out, VPIS);
  not not_7 (not_7_out, ZAKLENI);
  not not_8 (not_8_out, ERR);
  not not_9 (not_9_out, S2);
  not not_10 (not_10_out, ODKLENI);
  and and_4 (and_4_out, not_10_out, not_11_out, S0);
  not not_11 (not_11_out, ZAKLENI);
  and and_5 (and_5_out, ODKLENI, S1);
  or or_1 (S2_2, and_1_out, and_2_out, ERR, and_3_out);
  and and_6 (and_6_out, not_6_out, not_7_out, not_8_out, S1);
  and and_7 (and_7_out, ODKLENI, not_9_out);
  or or_2 (S1_2, and_6_out, and_7_out, and_8_out);
  and and_8 (and_8_out, ODKLENI, S0);
  or or_3 (S0_2, and_4_out, ERR, NAPREJ, and_5_out);
endmodule

module ALLOUTPUTS (
  input  VPIS,
  input  ODKLENI,
  input  ZAKLENI,
  input  NAPREJ,
  input  ERR,
  input  S2,
  input  S1,
  input  S0,
  output S2_2,
  output S1_2,
  output S0_2
);

  wire and_1_out, and_2_out, and_3_out, and_4_out, and_5_out, and_6_out, and_7_out, and_8_out, and_9_out,
       and_10_out, and_11_out, and_12_out, and_13_out, and_14_out, and_15_out, and_16_out, and_17_out,
       and_18_out, and_19_out, and_20_out, and_21_out, and_22_out, and_23_out, and_24_out, and_25_out,
       and_26_out, and_27_out, and_28_out, and_29_out, and_30_out, not_1_out, not_2_out, not_3_out,
       not_4_out, not_5_out, not_6_out, not_7_out, not_8_out, not_9_out, not_10_out, not_11_out, not_12_out,
       not_13_out, not_14_out, not_15_out, not_16_out, not_17_out, not_18_out, not_19_out, not_20_out,
       not_21_out, not_22_out, not_23_out, not_24_out, not_25_out, not_26_out, not_27_out, not_28_out,
       not_29_out, not_30_out, not_31_out, not_32_out, not_33_out, not_34_out, not_35_out, not_36_out,
       not_37_out, not_38_out, not_39_out, not_40_out, not_41_out, not_42_out, not_43_out, not_44_out,
       not_45_out, not_46_out, not_47_out;

  not not_1 (not_1_out, ODKLENI);
  not not_2 (not_2_out, ZAKLENI);
  not not_3 (not_3_out, ZAKLENI);
  not not_4 (not_4_out, S0);
  not not_5 (not_5_out, VPIS);
  not not_6 (not_6_out, ODKLENI);
  not not_7 (not_7_out, ZAKLENI);
  not not_8 (not_8_out, NAPREJ);
  not not_9 (not_9_out, S0);
  not not_10 (not_10_out, VPIS);
  not not_11 (not_11_out, ODKLENI);
  not not_12 (not_12_out, ZAKLENI);
  not not_13 (not_13_out, ERR);
  not not_14 (not_14_out, S1);
  not not_15 (not_15_out, VPIS);
  not not_16 (not_16_out, ZAKLENI);
  not not_17 (not_17_out, ERR);
  not not_18 (not_18_out, ERR);
  not not_19 (not_19_out, S0);
  not not_20 (not_20_out, S0);
  not not_21 (not_21_out, VPIS);
  not not_22 (not_22_out, ZAKLENI);
  not not_23 (not_23_out, NAPREJ);
  not not_24 (not_24_out, ERR);
  not not_25 (not_25_out, S2);
  not not_26 (not_26_out, S0);
  not not_27 (not_27_out, VPIS);
  not not_28 (not_28_out, ZAKLENI);
  not not_29 (not_29_out, NAPREJ);
  not not_30 (not_30_out, ERR);
  not not_31 (not_31_out, S0);
  not not_32 (not_32_out, ODKLENI);
  not not_33 (not_33_out, ZAKLENI);
  not not_34 (not_34_out, ZAKLENI);
  not not_35 (not_35_out, S2);
  not not_36 (not_36_out, S2);
  not not_37 (not_37_out, S1);
  not not_38 (not_38_out, VPIS);
  not not_39 (not_39_out, ODKLENI);
  not not_40 (not_40_out, ZAKLENI);
  not not_41 (not_41_out, NAPREJ);
  not not_42 (not_42_out, S2);
  not not_43 (not_43_out, VPIS);
  not not_44 (not_44_out, ODKLENI);
  not not_45 (not_45_out, ZAKLENI);
  not not_46 (not_46_out, ERR);
  not not_47 (not_47_out, S2);
  and and_1 (and_1_out, not_1_out, not_2_out, S2);
  and and_2 (and_2_out, not_3_out, S2, not_4_out);
  and and_3 (and_3_out, S2, S1);
  and and_4 (and_4_out, not_5_out, not_6_out, not_7_out, not_8_out, ERR, S1, not_9_out);
  and and_5 (and_5_out, ERR, S2);
  and and_6 (and_6_out, not_10_out, not_11_out, not_12_out, NAPREJ, not_13_out, not_14_out, S0);
  and and_7 (and_7_out, NAPREJ, S2);
  and and_8 (and_8_out, ODKLENI, ZAKLENI, S2);
  and and_9 (and_9_out, VPIS, S2);
  and and_10 (and_10_out, not_15_out, not_16_out, not_17_out, S1);
  and and_11 (and_11_out, not_18_out, S1, not_19_out);
  and and_12 (and_12_out, S2, S1);
  and and_13 (and_13_out, ERR, S1, S0);
  and and_14 (and_14_out, NAPREJ, S1);
  and and_15 (and_15_out, ZAKLENI, S1, not_20_out);
  and and_16 (and_16_out, not_21_out, ODKLENI, not_22_out, not_23_out, not_24_out, not_25_out, not_26_out);
  and and_17 (and_17_out, ODKLENI, S1);
  and and_18 (and_18_out, not_27_out, ODKLENI, not_28_out, not_29_out, not_30_out, S2, S0);
  and and_19 (and_19_out, VPIS, S1, not_31_out);
  and and_20 (and_20_out, VPIS, ZAKLENI, S1);
  and and_21 (and_21_out, not_32_out, not_33_out, S0);
  and and_22 (and_22_out, not_34_out, not_35_out, S0);
  and and_23 (and_23_out, not_36_out, not_37_out, S0);
  and and_24 (and_24_out, S2, S1, S0);
  and and_25 (and_25_out, ERR, S0);
  and and_26 (and_26_out, not_38_out, not_39_out, not_40_out, not_41_out, ERR, not_42_out, S1);
  and and_27 (and_27_out, NAPREJ, S0);
  and and_28 (and_28_out, not_43_out, not_44_out, not_45_out, NAPREJ, not_46_out, not_47_out, S1);
  and and_29 (and_29_out, ODKLENI, ZAKLENI, S0);
  and and_30 (and_30_out, VPIS, S0);
  or or_1 (S2_2, and_1_out, and_2_out, and_3_out, and_4_out, and_5_out, and_6_out, and_7_out, and_8_out, and_9_out);
  or or_2 (S1_2, and_10_out, and_11_out, and_12_out, and_13_out, and_14_out, and_15_out, and_16_out, and_17_out, and_18_out, and_19_out, and_20_out);
  or or_3 (S0_2, and_21_out, and_22_out, and_23_out, and_24_out, and_25_out, and_26_out, and_27_out, and_28_out, and_29_out, and_30_out);
endmodule

module ALLOUTPUTSFIXED (
  input  VPIS,
  input  ODKLENI,
  input  ZAKLENI,
  input  NAPREJ,
  input  ERR,
  input  S2,
  input  S1,
  input  S0,
  output S22,
  output S12,
  output S02
);

  wire and_1_out, and_2_out, and_3_out, and_4_out, and_5_out, and_6_out, and_7_out, and_8_out, and_9_out,
       and_10_out, and_11_out, and_12_out, and_13_out, and_14_out, and_15_out, and_16_out, and_17_out,
       and_18_out, and_19_out, and_20_out, and_21_out, and_22_out, and_23_out, and_24_out, and_25_out,
       and_26_out, and_27_out, and_28_out, and_29_out, and_30_out, and_31_out, not_1_out, not_2_out,
       not_3_out, not_4_out, not_5_out, not_6_out, not_7_out, not_8_out, not_9_out, not_10_out, not_11_out,
       not_12_out, not_13_out, not_14_out, not_15_out, not_16_out, not_17_out, not_18_out, not_19_out,
       not_20_out, not_21_out, not_22_out, not_23_out, not_24_out, not_25_out, not_26_out, not_27_out,
       not_28_out, not_29_out, not_30_out, not_31_out, not_32_out, not_33_out, not_34_out, not_35_out,
       not_36_out, not_37_out, not_38_out, not_39_out, not_40_out, not_41_out, not_42_out, not_43_out,
       not_44_out, not_45_out, not_46_out, not_47_out, not_48_out;

  not not_1 (not_1_out, ODKLENI);
  not not_2 (not_2_out, ZAKLENI);
  not not_3 (not_3_out, ZAKLENI);
  not not_4 (not_4_out, S0);
  not not_5 (not_5_out, VPIS);
  not not_6 (not_6_out, ODKLENI);
  not not_7 (not_7_out, ZAKLENI);
  not not_8 (not_8_out, NAPREJ);
  not not_9 (not_9_out, S0);
  not not_10 (not_10_out, VPIS);
  not not_11 (not_11_out, ODKLENI);
  not not_12 (not_12_out, ZAKLENI);
  not not_13 (not_13_out, ERR);
  not not_14 (not_14_out, S1);
  not not_15 (not_15_out, VPIS);
  not not_16 (not_16_out, ZAKLENI);
  not not_17 (not_17_out, ERR);
  not not_18 (not_18_out, ERR);
  not not_19 (not_19_out, S0);
  not not_20 (not_20_out, S0);
  not not_21 (not_21_out, VPIS);
  not not_22 (not_22_out, ZAKLENI);
  not not_23 (not_23_out, NAPREJ);
  not not_24 (not_24_out, ERR);
  not not_25 (not_25_out, S2);
  not not_26 (not_26_out, S0);
  not not_27 (not_27_out, VPIS);
  not not_28 (not_28_out, ZAKLENI);
  not not_29 (not_29_out, NAPREJ);
  not not_30 (not_30_out, ERR);
  not not_31 (not_31_out, S0);
  not not_32 (not_32_out, ODKLENI);
  not not_33 (not_33_out, ZAKLENI);
  not not_34 (not_34_out, NAPREJ);
  not not_35 (not_35_out, NAPREJ);
  not not_36 (not_36_out, S2);
  not not_37 (not_37_out, S1);
  not not_38 (not_38_out, VPIS);
  not not_39 (not_39_out, ODKLENI);
  not not_40 (not_40_out, ZAKLENI);
  not not_41 (not_41_out, NAPREJ);
  not not_42 (not_42_out, S2);
  not not_43 (not_43_out, VPIS);
  not not_44 (not_44_out, ODKLENI);
  not not_45 (not_45_out, ZAKLENI);
  not not_46 (not_46_out, ERR);
  not not_47 (not_47_out, S2);
  not not_48 (not_48_out, S2);
  and and_1 (and_1_out, not_1_out, not_2_out, S2);
  and and_2 (and_2_out, not_3_out, S2, not_4_out);
  and and_3 (and_3_out, S2, S1);
  and and_4 (and_4_out, not_5_out, not_6_out, not_7_out, not_8_out, ERR, S1, not_9_out);
  and and_5 (and_5_out, ERR, S2);
  and and_6 (and_6_out, not_10_out, not_11_out, not_12_out, NAPREJ, not_13_out, not_14_out, S0);
  and and_7 (and_7_out, NAPREJ, S2);
  and and_8 (and_8_out, ODKLENI, ZAKLENI, S2);
  and and_9 (and_9_out, VPIS, S2);
  and and_10 (and_10_out, not_15_out, not_16_out, not_17_out, S1);
  and and_11 (and_11_out, not_18_out, S1, not_19_out);
  and and_12 (and_12_out, S2, S1);
  and and_13 (and_13_out, ERR, S1, S0);
  and and_14 (and_14_out, NAPREJ, S1);
  and and_15 (and_15_out, ZAKLENI, S1, not_20_out);
  and and_16 (and_16_out, not_21_out, ODKLENI, not_22_out, not_23_out, not_24_out, not_25_out, not_26_out);
  and and_17 (and_17_out, ODKLENI, S1);
  and and_18 (and_18_out, not_27_out, ODKLENI, not_28_out, not_29_out, not_30_out, S2, S0);
  and and_19 (and_19_out, VPIS, S1, not_31_out);
  and and_20 (and_20_out, VPIS, ZAKLENI, S1);
  and and_21 (and_21_out, not_32_out, not_33_out, not_34_out, S0);
  and and_22 (and_22_out, not_35_out, not_36_out, not_37_out, S0);
  and and_23 (and_23_out, S2, S1, S0);
  and and_24 (and_24_out, ERR, S0);
  and and_25 (and_25_out, not_38_out, not_39_out, not_40_out, not_41_out, ERR, not_42_out, S1);
  and and_26 (and_26_out, not_43_out, not_44_out, not_45_out, NAPREJ, not_46_out, not_47_out, S1);
  and and_27 (and_27_out, NAPREJ, S2, S0);
  and and_28 (and_28_out, ZAKLENI, NAPREJ, S0);
  and and_29 (and_29_out, ODKLENI, not_48_out, S0);
  and and_30 (and_30_out, ODKLENI, ZAKLENI, S0);
  and and_31 (and_31_out, VPIS, S0);
  or or_1 (S22, and_1_out, and_2_out, and_3_out, and_4_out, and_5_out, and_6_out, and_7_out, and_8_out, and_9_out);
  or or_2 (S12, and_10_out, and_11_out, and_12_out, and_13_out, and_14_out, and_15_out, and_16_out, and_17_out, and_18_out, and_19_out, and_20_out);
  or or_3 (S02, and_21_out, and_22_out, and_23_out, and_24_out, and_25_out, and_26_out, and_27_out, and_28_out, and_29_out, and_30_out, and_31_out);
endmodule
