// Logisim project 1_Seminar2.circ as structural Verilog: 1 circuit, main circuit 1
module _1 (
  input  Change_this_to_1_to_Write,
  input  in_2,
  output out_3,
  output [3:0] out_4
);

  wire and_1_out, and_2_out, Clk_out, comparator_1_eq, comparator_1_gt, comparator_1_lt,
       controlled_buffer_2_out, counter_2_carry, keyboard_1_avail, not_1_out, O_out, or_1_out, or_2_out,
       Z_out;
  wire [2:0] counter_2_q;
  wire [6:0] keyboard_1_data;

  Button O (.out(O_out));
  Button K ();  // open: out
  Clock Clk (.out(Clk_out));
  assign out_3 = 1'b1 ? O_out : 1'bz;  // Controlled_Buffer controlled_buffer_1
  assign controlled_buffer_2_out = keyboard_1_avail ? Clk_out : 1'bz;  // Controlled_Buffer controlled_buffer_2
  Keyboard #(.buflen(4)) keyboard_1 (
    .clk(controlled_buffer_2_out), .avail(keyboard_1_avail), .data(keyboard_1_data));  // open: re, clr
  Comparator #(.width(4)) comparator_1 (
    .a(out_4), .b(keyboard_1_data[3:0]), .gt(comparator_1_gt), .eq(comparator_1_eq), .lt(comparator_1_lt));
  Counter #(.width(2), .max('h3)) counter_1 (.load(in_2), .clk(Clk_out));  // open: D, count, Q, carry, clr
  Counter #(.width(3), .max('h3)) counter_2 (
    .load(in_2), .count(comparator_1_eq), .Q(counter_2_q), .carry(counter_2_carry),
    .clk(controlled_buffer_2_out), .clr(Z_out));  // open: D
  or or_1 (or_1_out, comparator_1_gt, comparator_1_lt);
  and and_1 (and_1_out, or_1_out, keyboard_1_avail);
  Button Z (.out(Z_out));
  or or_2 (or_2_out, and_1_out, Z_out);
  RAM #(.addrWidth(2), .dataWidth(4)) ram_1 (
    .addr(counter_2_q[1:0]), .data(out_4), .sel(1'b1), .clk(Clk_out), .ld(Change_this_to_1_to_Write));  // open: clr
  not not_1 (not_1_out, Change_this_to_1_to_Write);
  assign out_4 = not_1_out ? keyboard_1_data[3:0] : 4'bz;  // Controlled_Buffer controlled_buffer_3
  and and_2 (and_2_out, not_1_out, counter_2_carry);
  LED K_veljavna (.in(and_2_out));
  TTY tty_1 (.data(keyboard_1_data), .clk(Clk_out));  // open: we, clr
  TTY tty_2 (.data({3'b000, out_4}), .clk(Clk_out));  // open: we, clr
  LED O_Z (.in(counter_2_carry));
  LED Err (.in(and_1_out));
endmodule
