// Logisim project 2_Seminar2_1.circ as structural Verilog: 1 circuit, main circuit 1
module _1 (
  input  in_1,
  output [3:0] out_2
);

  wire and_1_out, and_2_out, and_3_out, Clk_out, comparator_1_eq, comparator_1_gt, comparator_1_lt,
       controlled_buffer_1_out, counter_2_carry, keyboard_1_avail, not_1_out, not_2_out, Odkleni_out,
       or_1_out, or_2_out, or_3_out, register_1_q, register_2_q, \Vpiši_out , Z_out;
  wire [2:0] counter_2_q;
  wire [6:0] keyboard_1_data;

  Button \Vpiši  (.out(\Vpiši_out ));
  Button Odkleni (.out(Odkleni_out));
  Clock Clk (.out(Clk_out));
  Register #(.width(1)) register_1 (
    .D(not_1_out), .Q(register_1_q), .clk(or_1_out), .clr(counter_2_carry));  // open: en
  not not_1 (not_1_out, \Vpiši_out );
  or or_1 (or_1_out, \Vpiši_out , Odkleni_out);
  Register #(.width(1)) register_2 (.D(or_1_out), .Q(register_2_q), .clk(or_1_out), .clr(counter_2_carry));  // open: en
  assign controlled_buffer_1_out = keyboard_1_avail ? Clk_out : 1'bz;  // Controlled_Buffer controlled_buffer_1
  Keyboard #(.buflen(4)) keyboard_1 (
    .clk(and_1_out), .avail(keyboard_1_avail), .data(keyboard_1_data));  // open: re, clr
  and and_1 (and_1_out, register_2_q, controlled_buffer_1_out);
  Comparator #(.width(4)) comparator_1 (
    .a(out_2), .b(keyboard_1_data[3:0]), .gt(comparator_1_gt), .eq(comparator_1_eq), .lt(comparator_1_lt));
  Counter #(.width(2), .max('h3)) counter_1 (.load(in_1), .clk(Clk_out));  // open: D, count, Q, carry, clr
  Counter #(.width(3), .max('h3)) counter_2 (
    .load(in_1), .count(comparator_1_eq), .Q(counter_2_q), .carry(counter_2_carry), .clk(and_1_out),
    .clr(Z_out));  // open: D
  or or_2 (or_2_out, comparator_1_gt, comparator_1_lt);
  and and_2 (and_2_out, or_2_out, and_1_out);
  Button Z (.out(Z_out));
  or or_3 (or_3_out, and_2_out, Z_out);
  RAM #(.addrWidth(2), .dataWidth(4)) ram_1 (
    .addr(counter_2_q[1:0]), .data(out_2), .sel(1'b1), .clk(Clk_out), .ld(register_1_q));  // open: clr
  not not_2 (not_2_out, register_1_q);
  assign out_2 = not_2_out ? keyboard_1_data[3:0] : 4'bz;  // Controlled_Buffer controlled_buffer_2
  and and_3 (and_3_out, not_2_out, counter_2_carry);
  LED K_veljavna (.in(and_3_out));
  LED O_Z (.in(counter_2_carry));
  LED Err (.in(and_2_out));
endmodule
