// Logisim project 5_openSeOdpreZa1Cikel_tipkovnicaResetJeBedn_OstaloGood.circ as structural Verilog: 1 circuit, main circuit 1
module _1 (
  input  in_1
);

  wire and_1_out, and_2_out, and_3_out, Clk_out, comparator_1_eq, comparator_1_gt, comparator_1_lt,
       controlled_buffer_1_out, counter_1_carry, d_ff_1_q, keyboard_1_avail, not_1_out, not_2_out,
       Odkleni_out, or_1_out, or_2_out, or_3_out, register_1_q, register_2_q, register_3_q, \Vpiši_out ,
       Z_out;
  wire [2:0] counter_1_q;
  wire [3:0] controlled_buffer_2_out, keyboard_1_data_2;
  wire [6:4] keyboard_1_data;

  Button \Vpiši  (.out(\Vpiši_out ));
  Button Odkleni (.out(Odkleni_out));
  Button Z (.out(Z_out));
  not not_1 (not_1_out, \Vpiši_out );
  or or_1 (or_1_out, \Vpiši_out , Odkleni_out);
  Clock Clk (.out(Clk_out));
  Register #(.width(1)) register_1 (.D(not_1_out), .Q(register_1_q), .clk(or_1_out));  // open: en, clr
  Register #(.width(1)) register_2 (.D(Z_out), .Q(register_2_q), .clk(Z_out), .clr(d_ff_1_q));  // open: en
  Register #(.width(1)) register_3 (.D(or_1_out), .Q(register_3_q), .clk(or_1_out), .clr(d_ff_1_q));  // open: en
  assign controlled_buffer_1_out = keyboard_1_avail ? Clk_out : 1'bz;  // Controlled_Buffer controlled_buffer_1
  and and_1 (and_1_out, register_3_q, controlled_buffer_1_out);
  Comparator #(.width(4)) comparator_1 (
    .a(controlled_buffer_2_out), .b(keyboard_1_data_2), .gt(comparator_1_gt), .eq(comparator_1_eq),
    .lt(comparator_1_lt));
  Keyboard #(.buflen(4)) keyboard_1 (
    .clk(and_1_out), .clr(d_ff_1_q), .avail(keyboard_1_avail), .data({keyboard_1_data, keyboard_1_data_2}));  // open: re
  Counter #(.width(3), .max('h3)) counter_1 (
    .load(1'b0), .count(comparator_1_eq), .Q(counter_1_q), .carry(counter_1_carry), .clk(and_1_out),
    .clr(d_ff_1_q));  // open: D
  and and_2 (and_2_out, and_1_out, or_2_out);
  or or_2 (or_2_out, comparator_1_gt, comparator_1_lt);
  not not_2 (not_2_out, register_1_q);
  or or_3 (or_3_out, counter_1_carry, and_2_out, register_2_q);
  assign controlled_buffer_2_out = not_2_out ? keyboard_1_data_2 : 4'bz;  // Controlled_Buffer controlled_buffer_2
  RAM #(.addrWidth(2), .dataWidth(4)) ram_1 (
    .addr(counter_1_q[1:0]), .data(controlled_buffer_2_out), .sel(1'b1), .clk(and_1_out), .ld(register_1_q));  // open: clr
  D_Flip_Flop d_ff_1 (.clk(Clk_out), .D(or_3_out), .Q(d_ff_1_q), .en(1'b1));  // open: Qn, preset, reset
  and and_3 (and_3_out, not_2_out, counter_1_carry);
  LED K_veljavna (.in(and_3_out));
  LED O_Z (.in(counter_1_carry));
  LED Err (.in(and_2_out));

  // Notes on the sheet:
  //   Izbira operacije - se ne resetira ob koncu
  //   potek operacije - 1 - obratovanje vezja
  //   potek operacije - 1 -> obratovanje vezja
  //   Tipkovnica
  //   Določitev reseta - ob koncu avtomata, napaki ali zaklenitvi ključavnice
endmodule
