// Logisim project 6_Working.circ as structural Verilog: 1 circuit, main circuit 1
module _1 (
  output [3:0] out_1
);

  wire and_1_out, and_2_out, and_3_out, Clk_out, comparator_1_eq, comparator_1_gt, comparator_1_lt,
       counter_1_carry, d_ff_1_q, d_ff_2_q, keyboard_1_avail, not_1_out, not_2_out, Odkleni_out, or_1_out,
       or_2_out, or_3_out, or_4_out, or_5_out, register_1_q, register_2_q, register_3_q, register_4_q,
       register_5_q, register_6_q, \Vpiši_out , Z_out;
  wire [2:0] counter_1_q;
  wire [3:0] ram_1_data;
  wire [6:4] keyboard_1_data;

  Clock Clk (.out(Clk_out));
  Button \Vpiši  (.out(\Vpiši_out ));
  Button Odkleni (.out(Odkleni_out));
  Button Z (.out(Z_out));
  not not_1 (not_1_out, \Vpiši_out );
  or or_1 (or_1_out, \Vpiši_out , Odkleni_out);
  Register #(.width(1)) register_1 (.D(not_1_out), .Q(register_1_q), .clk(or_1_out), .clr(or_5_out));  // open: en
  Register #(.width(1)) register_2 (.D(Z_out), .Q(register_2_q), .clk(Z_out), .clr(or_5_out));  // open: en
  or or_2 (or_2_out, or_1_out, Z_out);
  Register #(.width(1)) register_3 (.D(or_1_out), .Q(register_3_q), .clk(or_1_out), .clr(or_5_out));  // open: en
  and and_1 (and_1_out, keyboard_1_avail, Clk_out, register_3_q);
  Comparator #(.width(4)) comparator_1 (
    .a(ram_1_data), .b(out_1), .gt(comparator_1_gt), .eq(comparator_1_eq), .lt(comparator_1_lt));
  Keyboard #(.buflen(4)) keyboard_1 (
    .clk(and_1_out), .clr(or_5_out), .avail(keyboard_1_avail), .data({keyboard_1_data, out_1}));  // open: re
  D_Flip_Flop d_ff_1 (.clk(Clk_out), .D(keyboard_1_avail), .Q(d_ff_1_q), .en(1'b1));  // open: Qn, preset, reset
  Counter #(.width(3), .max('h4)) counter_1 (
    .load(1'b0), .count(comparator_1_eq), .Q(counter_1_q), .carry(counter_1_carry), .clk(and_1_out),
    .clr(or_5_out));  // open: D
  or or_3 (or_3_out, comparator_1_gt, comparator_1_lt);
  and and_2 (and_2_out, keyboard_1_avail, register_1_q, or_3_out);
  not not_2 (not_2_out, register_1_q);
  or or_4 (or_4_out, and_2_out, register_2_q);
  RAM #(.addrWidth(2), .dataWidth(4)) ram_1 (
    .addr(counter_1_q[1:0]), .data(ram_1_data), .sel(1'b1), .clk(and_1_out), .ld(register_1_q));  // open: clr
  assign ram_1_data = not_2_out ? out_1 : 4'bz;  // Controlled_Buffer controlled_buffer_1
  D_Flip_Flop d_ff_2 (.clk(Clk_out), .D(or_4_out), .Q(d_ff_2_q), .en(1'b1));  // open: Qn, preset, reset
  Register #(.width(1)) register_4 (
    .D(counter_1_carry), .Q(register_4_q), .clk(counter_1_carry), .clr(d_ff_2_q));  // open: en
  or or_5 (or_5_out, counter_1_carry, d_ff_2_q);
  LED O_Z (.in(register_4_q));
  Register #(.width(1)) register_5 (.D(d_ff_2_q), .Q(register_5_q), .clk(d_ff_2_q), .clr(or_2_out));  // open: en
  and and_3 (and_3_out, not_2_out, counter_1_carry, register_4_q);
  Register #(.width(1)) register_6 (.D(and_3_out), .Q(register_6_q), .clk(and_3_out), .clr(or_2_out));  // open: en
  LED Err (.in(register_5_q));
  LED K_veljavna (.in(register_6_q));

  // Notes on the sheet:
  //   potek operacije - 1 - obratovanje vezja
  //   potek operacije - 1 -> obratovanje vezja
  //   Tipkovnica
  //   Določitev reseta - ob koncu avtomata, napaki ali zaklenitvi ključavnice
endmodule
